// Logisim project ISA.circ as structural Verilog: 1 circuit, main circuit my circuit
module my_circuit (
  input  in_1,
  input  in_2,
  input  LD_PC,
  input  LD_MAR,
  output out_5,
  output [31:0] out_6
);

  wire [31:0] adder_1_out, PC_q;

  Adder #(.width(32)) adder_1 (.a(PC_q), .b(32'h4), .out(adder_1_out));  // open: cin, cout
  Register #(.width(32)) PC (.D(adder_1_out), .en(LD_PC), .Q(PC_q), .clk(in_1));  // open: clr
  Register #(.width(32)) MAR (.D(PC_q), .en(LD_MAR), .Q(out_6), .clk(in_1));  // open: clr

  assign out_5 = in_2;

  // Other names for the same wires on the sheet: CK = in_1
endmodule
